// Logisim project cpu-final.circ as structural Verilog: 10 circuits, main circuit main
module main (
  output RegWrite,
  output RegDst,
  output Jump,
  output ALUSrc,
  output MemRead,
  output MemWrite,
  output [2:0] opcode,
  output rd,
  output rs,
  output [4:0] immediate,
  output rt,
  output MemtoReg,
  output [2:0] funct,
  output [3:0] adddress,
  output branch,
  output [8:0] out_16,
  output [8:0] out_17,
  output [8:0] out_18,
  output [8:0] out_19
);

  wire alu_1_yesbranch, and_1_out, clock_1_out, clock_2_out, control_1_alu_enable, control_1_rtype,
       multiplexer_1_out;
  wire [8:0] _00_q, adder_1_out, adder_2_out, bit_extender_1_out, bit_extender_2_out, multiplexer_3_out,
       multiplexer_4_out, multiplexer_5_out, ram_1_data;

  Register #(.width(9)) _00 (.D(multiplexer_5_out), .Q(_00_q), .clk(clock_1_out));  // open: en, clr
  Clock clock_1 (.out(clock_1_out));
  ROM #(.addrWidth(9), .dataWidth(9)) rom_1 (.addr(_00_q), .data({opcode, rd, immediate[4], adddress}));  // open: sel
  Multiplexer #(.enable("false")) multiplexer_1 (.in0(rd), .in1(immediate[4]), .out(multiplexer_1_out), .sel(RegDst));
  Registers registers_1 (
    .Data_In(multiplexer_3_out), .Read_Reg_1(out_16), .Read_Reg_2(out_18), .Read_Select_1(multiplexer_1_out),
    .R_Select_2(adddress[3]), .Register_Select(rd), .Write(RegWrite));
  alu alu_1 (
    .In_A(out_16), .In_B(out_18), .Op_Select(adddress[1:0]), .Output(out_19), .YESBRANCH(alu_1_yesbranch),
    .branch(branch), .in_1(control_1_alu_enable));
  assign bit_extender_1_out = {{4{1'b0}}, {immediate[4], adddress}};  // Bit_Extender bit_extender_1
  assign bit_extender_2_out = {{5{1'b0}}, adddress};  // Bit_Extender bit_extender_2
  Multiplexer #(.width(9), .enable("false")) multiplexer_2 (
    .in0(bit_extender_1_out), .in1(out_19), .out(out_17), .sel(control_1_rtype));
  control control_1 (
    .opcode(opcode), .rtype(control_1_rtype), .RegWrite(RegWrite), .RegDst(RegDst), .Jump(Jump),
    .ALUSrc(ALUSrc), .MemRead(MemRead), .MemWrite(MemWrite), .MemtoReg(MemtoReg), .branch(branch),
    .ALU_enable(control_1_alu_enable));
  RAM #(.addrWidth(9), .dataWidth(9), .bus("separate")) ram_1 (
    .addr(bit_extender_2_out), .din(out_17), .data(ram_1_data), .str(MemWrite), .clk(clock_2_out),
    .ld(MemRead));  // open: sel, clr
  Clock clock_2 (.out(clock_2_out));
  Multiplexer #(.width(9), .enable("false")) multiplexer_3 (
    .in0(out_17), .in1(ram_1_data), .out(multiplexer_3_out), .sel(MemtoReg));
  Adder #(.width(9)) adder_1 (.a(_00_q), .b(9'h1), .out(adder_1_out));  // open: cin, cout
  and and_1 (and_1_out, branch, alu_1_yesbranch);
  Adder #(.width(9)) adder_2 (.a(adder_1_out), .b(bit_extender_2_out), .out(adder_2_out));  // open: cin, cout
  Multiplexer #(.width(9), .enable("false")) multiplexer_4 (
    .in0(adder_1_out), .in1(adder_2_out), .out(multiplexer_4_out), .sel(and_1_out));
  Multiplexer #(.width(9), .enable("false")) multiplexer_5 (
    .in0(multiplexer_4_out), .in1(bit_extender_2_out), .out(multiplexer_5_out), .sel(Jump));

  assign funct = adddress[2:0];
  assign immediate[3:0] = adddress;
  assign rs = immediate[4];
  assign rt = adddress[3];

  // Notes on the sheet:
  //   WHAT ARE WE DOING TODAY BOB
  //   contents of rom_1 (hex, n*v repeats v):
  //   42 1c0 101 121 10 c1 192 1c0 1c0 c0 104 a0 9 c3
  //   WOW
  //   ~MATH WORLD~
  //   MEMORY CORNER
  //   BRANCH?
endmodule

module _9_bit_AND (
  input  [8:0] in_1,
  input  [8:0] in_2,
  output [8:0] out_3
);

  and and_1 (out_3[0], in_1[0], in_2[0]);
  and and_2 (out_3[1], in_1[1], in_2[1]);
  and and_3 (out_3[2], in_1[2], in_2[2]);
  and and_4 (out_3[3], in_1[3], in_2[3]);
  and and_5 (out_3[4], in_1[4], in_2[4]);
  and and_6 (out_3[5], in_1[5], in_2[5]);
  and and_7 (out_3[6], in_1[6], in_2[6]);
  and and_8 (out_3[7], in_1[7], in_2[7]);
  and and_9 (out_3[8], in_1[8], in_2[8]);
endmodule

module alu (
  input  in_1,
  input  [1:0] Op_Select,
  input  [8:0] In_A,
  input  [8:0] In_B,
  input  branch,
  output [8:0] Output,
  output YESBRANCH
);

  wire nor_1_out;
  wire [8:0] adder_1_out, multiplexer_1_out, n9_bit_and_1_out_3, n9_bit_or_1_out_3, subtractor_1_out,
       subtractor_2_out;

  Subtractor #(.width(9)) subtractor_1 (.a(In_A), .b(In_B), .out(subtractor_1_out));  // open: bin, bout
  Adder #(.width(9)) adder_1 (.a(In_A), .b(In_B), .out(adder_1_out));  // open: cin, cout
  Subtractor #(.width(9)) subtractor_2 (.a(In_A), .b(In_B), .out(subtractor_2_out));  // open: bin, bout
  _9_bit_AND u_9_bit_and_1 (.in_1(In_A), .in_2(In_B), .out_3(n9_bit_and_1_out_3));
  _9_bit_OR u_9_bit_or_1 (.in_1(In_A), .in_2(In_B), .out_3(n9_bit_or_1_out_3));
  Multiplexer #(.select(2), .width(9), .disabled(0), .enable("false")) multiplexer_1 (
    .in0(adder_1_out), .in1(subtractor_2_out), .in2(n9_bit_and_1_out_3), .in3(n9_bit_or_1_out_3),
    .out(multiplexer_1_out), .sel(Op_Select));
  nor nor_1 (nor_1_out, subtractor_1_out[0], subtractor_1_out[1], subtractor_1_out[2], subtractor_1_out[3], subtractor_1_out[4], subtractor_1_out[5], subtractor_1_out[6], subtractor_1_out[7], subtractor_1_out[8]);
  and and_1 (YESBRANCH, branch, nor_1_out);
  Multiplexer #(.width(9), .enable("false")) multiplexer_2 (
    .in0(In_A), .in1(multiplexer_1_out), .out(Output), .sel(in_1));
endmodule

module _9_bit_OR (
  input  [8:0] in_1,
  input  [8:0] in_2,
  output [8:0] out_3
);

  or or_1 (out_3[0], in_1[0], in_2[0]);
  or or_2 (out_3[1], in_1[1], in_2[1]);
  or or_3 (out_3[2], in_1[2], in_2[2]);
  or or_4 (out_3[3], in_1[3], in_2[3]);
  or or_5 (out_3[4], in_1[4], in_2[4]);
  or or_6 (out_3[5], in_1[5], in_2[5]);
  or or_7 (out_3[6], in_1[6], in_2[6]);
  or or_8 (out_3[7], in_1[7], in_2[7]);
  or or_9 (out_3[8], in_1[8], in_2[8]);
endmodule

module Registers (
  input  Write,
  input  Read_Select_1,
  input  R_Select_2,
  input  [8:0] Data_In,
  input  Register_Select,
  output [8:0] Read_Reg_1,
  output [8:0] Read_Reg_2
);

  wire and_1_out, and_2_out, clock_1_out, clock_2_out, decoder_1_out0, decoder_1_out1;
  wire [8:0] R0_q, R1_q;

  Decoder #(.enable("false")) decoder_1 (.out0(decoder_1_out0), .out1(decoder_1_out1), .sel(Register_Select));
  Register #(.width(9)) R0 (.D(Data_In), .en(and_1_out), .Q(R0_q), .clk(clock_1_out));  // open: clr
  and and_1 (and_1_out, Write, decoder_1_out0);
  Clock clock_1 (.out(clock_1_out));
  Register #(.width(9)) R1 (.D(Data_In), .en(and_2_out), .Q(R1_q), .clk(clock_2_out));  // open: clr
  and and_2 (and_2_out, Write, decoder_1_out1);
  Clock clock_2 (.out(clock_2_out));
  Multiplexer #(.width(9), .enable("false")) multiplexer_1 (
    .in0(R0_q), .in1(R1_q), .out(Read_Reg_1), .sel(Read_Select_1));
  Multiplexer #(.width(9), .enable("false")) multiplexer_2 (.in0(R0_q), .in1(R1_q), .out(Read_Reg_2), .sel(R_Select_2));
endmodule

module itype (
  input  [2:0] opcode,
  output MemRead,
  output MemWrite,
  output MemtoReg,
  output branch,
  output load_immediate
);

  wire not_1_out, not_2_out, not_3_out, not_4_out;

  not not_1 (not_1_out, opcode[0]);
  not not_2 (not_2_out, opcode[1]);
  not not_3 (not_3_out, opcode[1]);
  nor sw (MemWrite, not_1_out, not_2_out, opcode[2]);
  nor lw (MemRead, opcode[0], not_3_out, opcode[2]);
  and and_1 (branch, opcode[2], opcode[1]);
  not not_4 (not_4_out, branch);
  and and_2 (load_immediate, opcode[2], not_4_out);

  assign MemtoReg = MemRead;
endmodule

module control (
  input  [2:0] opcode,
  output rtype,
  output RegWrite,
  output RegDst,
  output Jump,
  output ALUSrc,
  output MemRead,
  output MemWrite,
  output MemtoReg,
  output branch,
  output ALU_enable
);

  wire and_3_out, itype_1_branch, itype_1_load_immediate, nand_1_out, not_1_out, not_2_out, not_3_out,
       not_4_out, not_5_out, or_4_out, type_1_i, type_1_noop, type_1_r;

  or or_1 (rtype, type_1_r, MemWrite);
  \type  type_1 (.opcode(opcode), .R(type_1_r), .I(type_1_i), .Jump(Jump), .noop(type_1_noop));
  itype itype_1 (
    .opcode(opcode), .MemRead(MemRead), .MemWrite(MemWrite), .MemtoReg(MemtoReg), .branch(itype_1_branch),
    .load_immediate(itype_1_load_immediate));
  nand nand_1 (nand_1_out, type_1_i, MemWrite);
  or or_2 (RegDst, type_1_r, itype_1_load_immediate);
  and and_1 (branch, itype_1_branch, not_1_out);
  not not_1 (not_1_out, type_1_noop);
  or or_3 (ALU_enable, RegDst, itype_1_load_immediate);
  or or_4 (or_4_out, type_1_r, nand_1_out);
  not not_2 (not_2_out, Jump);
  and and_2 (ALUSrc, type_1_i, not_3_out);
  not not_3 (not_3_out, branch);
  not not_4 (not_4_out, type_1_noop);
  and and_3 (and_3_out, or_4_out, not_2_out);
  not not_5 (not_5_out, branch);
  and and_4 (RegWrite, not_4_out, not_5_out, and_3_out);
endmodule

module \type  (
  input  [2:0] opcode,
  output R,
  output I,
  output Jump,
  output noop
);

  wire nor_3_out, not_1_out, not_2_out;

  not not_1 (not_1_out, opcode[0]);
  and and_1 (noop, opcode[1], opcode[2], opcode[0]);
  nor nor_1 (Jump, opcode[1], not_1_out);
  nor nor_2 (R, opcode[2], opcode[1], opcode[0]);
  nor nor_3 (nor_3_out, R, Jump);
  and and_2 (I, nor_3_out, not_2_out);
  not not_2 (not_2_out, noop);
endmodule

module _2bitop (
  input  [8:0] in_1,
  output [1:0] out_2,
  output [5:0] out_3,
  output rs,
  output rt,
  output [4:0] address
);


  assign address = in_1[4:0];
  assign out_2 = in_1[8:7];
  assign out_3 = in_1[5:0];
  assign rs = in_1[6];
  assign rt = in_1[5];
endmodule

module _3bitop (
  input  [8:0] in_1
);
endmodule
