// Logisim project cpu.circ as structural Verilog: 10 circuits, main circuit main
module main (
  input  [8:0] in_1,
  input  [8:0] in_2,
  output RegWrite,
  output [8:0] out_4,
  output RegDst,
  output [8:0] out_6,
  output Jump,
  output ALUSrc,
  output MemRead,
  output MemWrite,
  output [2:0] opcode,
  output rd,
  output rs,
  output [4:0] immediate,
  output rt,
  output MemtoReg,
  output [2:0] funct,
  output [3:0] adddress,
  output branch,
  output [8:0] out_20,
  output [8:0] out_21,
  output [8:0] out_22,
  output [8:0] out_23,
  output [4:0] immediate_2,
  output [2:0] funct_2,
  output rs_2,
  output rt_2,
  output rd_2,
  output [3:0] address,
  output RegWrite_2,
  output ALU_enable,
  output RegDst_2,
  output branch_2,
  output MemtoReg_2,
  output Jump_2,
  output ALUSrc_2,
  output MemWrite_2,
  output MemRead_2
);

  wire clock_1_out, clock_2_out;
  wire [8:0] _00_q, adder_2_out, alu_1_output, alu_2_output, bit_extender_1_out, bit_extender_3_out,
       multiplexer_1_out, multiplexer_3_out, multiplexer_4_out, ram_1_data, registers_1_read_reg_2,
       registers_2_read_reg_1, registers_2_read_reg_2;
  wire [8:6] rom_2_data;

  Register #(.width(9)) _00 (.D(out_4), .Q(_00_q), .clk(clock_1_out));  // open: en, clr
  Clock clock_1 (.out(clock_1_out));
  ROM #(.addrWidth(9), .dataWidth(9)) rom_1 (.addr(_00_q), .data({opcode, rd, immediate[4], adddress}));  // open: sel
  ROM #(.addrWidth(9), .dataWidth(9)) rom_2 (.data({rom_2_data, rs_2, immediate_2[4], address}));  // open: addr, sel
  control control_1 (
    .opcode(rom_2_data), .RegWrite(RegWrite_2), .RegDst(RegDst_2), .Jump(Jump_2), .ALUSrc(ALUSrc_2),
    .MemRead(MemRead_2), .MemWrite(MemWrite_2), .MemtoReg(MemtoReg_2), .branch(branch_2),
    .ALU_enable(ALU_enable));
  Registers registers_1 (
    .Data_In(multiplexer_3_out), .Read_Reg_1(out_23), .Read_Reg_2(registers_1_read_reg_2),
    .Read_Select_1(immediate[4]), .R_Select_2(adddress[3]), .Register_Select(rd), .Write(RegWrite));
  alu alu_1 (.In_A(out_23), .In_B(multiplexer_1_out), .Op_Select(adddress[1:0]), .Output(alu_1_output));
  Multiplexer #(.width(9), .enable("false")) multiplexer_1 (
    .in0(registers_1_read_reg_2), .in1(out_22), .out(multiplexer_1_out), .sel(ALUSrc));
  Registers registers_2 (
    .Data_In(bit_extender_1_out), .Read_Reg_1(registers_2_read_reg_1), .Read_Reg_2(registers_2_read_reg_2),
    .Read_Select_1(rs_2), .R_Select_2(immediate_2[4]), .Register_Select(address[3]), .Write(RegWrite_2));
  alu alu_2 (
    .In_A(registers_2_read_reg_1), .In_B(registers_2_read_reg_2), .Op_Select(address[1:0]),
    .Output(alu_2_output));
  // Buffer buffer_1 is placed but not wired
  assign bit_extender_1_out = {{4{1'b0}}, {immediate_2[4], address}};  // Bit_Extender bit_extender_1
  assign out_22 = {{4{1'b0}}, {immediate[4], adddress}};  // Bit_Extender bit_extender_2
  assign bit_extender_3_out = {{5{1'b0}}, adddress};  // Bit_Extender bit_extender_3
  Multiplexer #(.width(9), .enable("false")) multiplexer_2 (
    .in0(alu_1_output), .in1(out_22), .out(out_20), .sel(ALUSrc));
  control control_2 (
    .opcode(opcode), .RegWrite(RegWrite), .RegDst(RegDst), .Jump(Jump), .ALUSrc(ALUSrc), .MemRead(MemRead),
    .MemWrite(MemWrite), .MemtoReg(MemtoReg), .branch(branch));  // open: ALU_enable
  RAM #(.addrWidth(9), .dataWidth(9), .bus("separate")) ram_1 (
    .addr(bit_extender_3_out), .din(out_20), .data(ram_1_data), .str(MemWrite), .clk(clock_2_out),
    .ld(MemRead));  // open: sel, clr
  Clock clock_2 (.out(clock_2_out));
  Multiplexer #(.width(9), .enable("false")) multiplexer_3 (
    .in0(out_20), .in1(ram_1_data), .out(multiplexer_3_out), .sel(MemtoReg));
  Adder #(.width(9)) adder_1 (.a(_00_q), .b(9'h1), .out(out_6));  // open: cin, cout
  Adder #(.width(9)) adder_2 (.a(out_6), .b(bit_extender_3_out), .out(adder_2_out));  // open: cin, cout
  Multiplexer #(.width(9), .enable("false")) multiplexer_4 (
    .in0(out_6), .in1(adder_2_out), .out(multiplexer_4_out), .sel(branch));
  Multiplexer #(.width(9), .enable("false")) multiplexer_5 (
    .in0(multiplexer_4_out), .in1(bit_extender_3_out), .out(out_4), .sel(Jump));

  assign funct = adddress[2:0];
  assign funct_2 = address[2:0];
  assign immediate[3:0] = adddress;
  assign immediate_2[3:0] = address;
  assign out_21 = out_20;
  assign rd_2 = address[3];
  assign rs = immediate[4];
  assign rt = adddress[3];
  assign rt_2 = immediate_2[4];

  // Notes on the sheet:
  //   WHAT ARE WE DOING TODAY BOB
  //   contents of rom_1 (hex, n*v repeats v):
  //   121 102 e0
  //   WOW
  //   contents of rom_2 (hex, n*v repeats v):
  //   180 1a1
  //   MATH WORLD
  //   MEMORY CORNER
  //   BRANCH?
endmodule

module _9_bit_AND (
  input  [8:0] in_1,
  input  [8:0] in_2,
  output [8:0] out_3
);

  and and_1 (out_3[0], in_1[0], in_2[0]);
  and and_2 (out_3[1], in_1[1], in_2[1]);
  and and_3 (out_3[2], in_1[2], in_2[2]);
  and and_4 (out_3[3], in_1[3], in_2[3]);
  and and_5 (out_3[4], in_1[4], in_2[4]);
  and and_6 (out_3[5], in_1[5], in_2[5]);
  and and_7 (out_3[6], in_1[6], in_2[6]);
  and and_8 (out_3[7], in_1[7], in_2[7]);
  and and_9 (out_3[8], in_1[8], in_2[8]);
endmodule

module alu (
  input  [1:0] Op_Select,
  input  [8:0] In_A,
  input  [8:0] In_B,
  output [8:0] Output
);

  wire [8:0] adder_1_out, n9_bit_and_1_out_3, n9_bit_or_1_out_3, subtractor_1_out;

  Adder #(.width(9)) adder_1 (.a(In_A), .b(In_B), .out(adder_1_out));  // open: cin, cout
  Subtractor #(.width(9)) subtractor_1 (.a(In_A), .b(In_B), .out(subtractor_1_out));  // open: bin, bout
  _9_bit_AND u_9_bit_and_1 (.in_1(In_A), .in_2(In_B), .out_3(n9_bit_and_1_out_3));
  _9_bit_OR u_9_bit_or_1 (.in_1(In_A), .in_2(In_B), .out_3(n9_bit_or_1_out_3));
  Multiplexer #(.select(2), .width(9), .disabled(0), .enable("false")) multiplexer_1 (
    .in0(adder_1_out), .in1(subtractor_1_out), .in2(n9_bit_and_1_out_3), .in3(n9_bit_or_1_out_3),
    .out(Output), .sel(Op_Select));
endmodule

module _9_bit_OR (
  input  [8:0] in_1,
  input  [8:0] in_2,
  output [8:0] out_3
);

  or or_1 (out_3[0], in_1[0], in_2[0]);
  or or_2 (out_3[1], in_1[1], in_2[1]);
  or or_3 (out_3[2], in_1[2], in_2[2]);
  or or_4 (out_3[3], in_1[3], in_2[3]);
  or or_5 (out_3[4], in_1[4], in_2[4]);
  or or_6 (out_3[5], in_1[5], in_2[5]);
  or or_7 (out_3[6], in_1[6], in_2[6]);
  or or_8 (out_3[7], in_1[7], in_2[7]);
  or or_9 (out_3[8], in_1[8], in_2[8]);
endmodule

module Registers (
  input  Write,
  input  Read_Select_1,
  input  R_Select_2,
  input  [8:0] Data_In,
  input  Register_Select,
  output [8:0] Read_Reg_1,
  output [8:0] Read_Reg_2
);

  wire and_1_out, and_2_out, clock_1_out, clock_2_out, decoder_1_out0, decoder_1_out1;
  wire [8:0] R0_q, R1_q;

  Decoder #(.enable("false")) decoder_1 (.out0(decoder_1_out0), .out1(decoder_1_out1), .sel(Register_Select));
  Register #(.width(9)) R0 (.D(Data_In), .en(and_1_out), .Q(R0_q), .clk(clock_1_out));  // open: clr
  and and_1 (and_1_out, Write, decoder_1_out0);
  Clock clock_1 (.out(clock_1_out));
  Register #(.width(9)) R1 (.D(Data_In), .en(and_2_out), .Q(R1_q), .clk(clock_2_out));  // open: clr
  and and_2 (and_2_out, Write, decoder_1_out1);
  Clock clock_2 (.out(clock_2_out));
  Multiplexer #(.width(9), .enable("false")) multiplexer_1 (
    .in0(R0_q), .in1(R1_q), .out(Read_Reg_1), .sel(Read_Select_1));
  Multiplexer #(.width(9), .enable("false")) multiplexer_2 (.in0(R0_q), .in1(R1_q), .out(Read_Reg_2), .sel(R_Select_2));
endmodule

module itype (
  input  [2:0] opcode,
  output MemRead,
  output MemWrite,
  output MemtoReg,
  output branch,
  output load_immediate
);

  wire not_1_out, not_2_out, not_3_out, not_4_out;

  not not_1 (not_1_out, opcode[0]);
  not not_2 (not_2_out, opcode[1]);
  not not_3 (not_3_out, opcode[1]);
  nor sw (MemWrite, not_1_out, not_2_out, opcode[2]);
  nor lw (MemRead, opcode[0], not_3_out, opcode[2]);
  and and_1 (branch, opcode[2], opcode[1]);
  not not_4 (not_4_out, branch);
  and and_2 (load_immediate, opcode[2], not_4_out);

  assign MemtoReg = MemRead;
endmodule

module control (
  input  [2:0] opcode,
  output RegWrite,
  output RegDst,
  output Jump,
  output ALUSrc,
  output MemRead,
  output MemWrite,
  output MemtoReg,
  output branch,
  output ALU_enable
);

  wire and_2_out, itype_1_branch, itype_1_load_immediate, nand_1_out, not_1_out, not_2_out, not_3_out,
       or_3_out, type_1_noop, type_1_r;

  \type  type_1 (.opcode(opcode), .R(type_1_r), .I(ALUSrc), .Jump(Jump), .noop(type_1_noop));
  itype itype_1 (
    .opcode(opcode), .MemRead(MemRead), .MemWrite(MemWrite), .MemtoReg(MemtoReg), .branch(itype_1_branch),
    .load_immediate(itype_1_load_immediate));
  nand nand_1 (nand_1_out, ALUSrc, MemWrite);
  or or_1 (RegDst, type_1_r, itype_1_load_immediate);
  and and_1 (branch, itype_1_branch, not_1_out);
  not not_1 (not_1_out, type_1_noop);
  or or_2 (ALU_enable, RegDst, itype_1_load_immediate);
  or or_3 (or_3_out, type_1_r, nand_1_out);
  not not_2 (not_2_out, Jump);
  not not_3 (not_3_out, type_1_noop);
  and and_2 (and_2_out, or_3_out, not_2_out);
  and and_3 (RegWrite, not_3_out, and_2_out);
endmodule

module \type  (
  input  [2:0] opcode,
  output R,
  output I,
  output Jump,
  output noop
);

  wire nor_3_out, not_1_out, not_2_out;

  not not_1 (not_1_out, opcode[0]);
  and and_1 (noop, opcode[1], opcode[2], opcode[0]);
  nor nor_1 (Jump, opcode[1], not_1_out);
  nor nor_2 (R, opcode[2], opcode[1], opcode[0]);
  nor nor_3 (nor_3_out, R, Jump);
  and and_2 (I, nor_3_out, not_2_out);
  not not_2 (not_2_out, noop);
endmodule

module _2bitop (
  input  [8:0] in_1,
  output [1:0] out_2,
  output [5:0] out_3,
  output rs,
  output rt,
  output [4:0] address
);


  assign address = in_1[4:0];
  assign out_2 = in_1[8:7];
  assign out_3 = in_1[5:0];
  assign rs = in_1[6];
  assign rt = in_1[5];
endmodule

module _3bitop (
  input  [8:0] in_1
);
endmodule
